# Fritzing sketch chess_board (saved by Fritzing 0.9.3b)
breadboards: 1

parts:
  U1 = 74HC4052 [package=dil16]
  Part1 = Arduino Uno (Rev3) - ICSP
  U2 = 74HC4052 [package=dil16]
  R1 = Resistor [tolerance=±5% resistance=2k package="0603 [SMD]"]

nets:
  VCC: U1.Y0, U1.Y, U1.X1, U1.VCC, Part1.5V, U2.Y0
  N1: U1.Y2, U1.X2
  N2: U1.Y3, U1.X
  N3: U1.Y1, U1.X0
  GND: U1.INH, U1.GND, U1.B, U1.X3, Part1.GND, Part1.D8, Part1.D10_PWM/SS, U2.INH, U2.GND, R1.Pin_0
  N4: U1.VEE, U1.A, Part1.D9_PWM
  N5: Part1.A0, U2.Y, R1.Pin_1
  N6: Part1.D5_PWM, U2.B
  N7: Part1.D6_PWM, U2.VEE
  N8: Part1.D7, U2.X3
